// Logisim project 8bitComputer.circ as structural Verilog: 7 circuits, main circuit main
module main (
  input  Ready,
  input  Ready_2,
  input  [7:0] Input_Port,
  output [7:0] Output_Port
);

  wire clock_1_out, cpu_1_wrmemory, cpu_1_wroutput, demultiplexer_1_out1, demultiplexer_1_out2;
  wire [1:0] cpu_1_dbussel;
  wire [7:0] controlled_buffer_3_out, cpu_1_abus, cpu_1_dbusout, ram_1_data;

  Clock clock_1 (.out(clock_1_out));
  Demultiplexer #(.select(2), .enable("false")) demultiplexer_1 (
    .out1(demultiplexer_1_out1), .out2(demultiplexer_1_out2), .in(1'b1), .sel(cpu_1_dbussel));  // open: out0, out3
  CPU cpu_1 (
    .InRdy(Ready), .OutRdy(Ready_2), .abus(cpu_1_abus), .wrMemory(cpu_1_wrmemory), .wrOutput(cpu_1_wroutput),
    .dbusout(cpu_1_dbusout), .dbusin(cpu_1_dbusout), .dbussel(cpu_1_dbussel), .Clk(clock_1_out));
  assign cpu_1_dbusout = demultiplexer_1_out1 ? Input_Port : 8'bz;  // Controlled_Buffer controlled_buffer_1
  assign Output_Port = cpu_1_wroutput ? cpu_1_dbusout : 8'bz;  // Controlled_Buffer controlled_buffer_2
  assign controlled_buffer_3_out = cpu_1_wrmemory ? cpu_1_dbusout : 8'bz;  // Controlled_Buffer controlled_buffer_3
  assign cpu_1_dbusout = demultiplexer_1_out2 ? ram_1_data : 8'bz;  // Controlled_Buffer controlled_buffer_4
  RAM #(.bus("separate")) ram_1 (
    .addr(cpu_1_abus), .din(controlled_buffer_3_out), .data(ram_1_data), .str(cpu_1_wrmemory), .sel(1'b1),
    .clk(clock_1_out), .ld(demultiplexer_1_out2));  // open: clr

  // Notes on the sheet:
  //   Addressbus
  //   Datenbus
endmodule

module CPU (
  input  InRdy,
  input  OutRdy,
  input  [7:0] dbusin,
  input  Clk,
  output [7:0] abus,
  output wrMemory,
  output wrOutput,
  output [7:0] dbusout,
  output [1:0] dbussel
);

  wire alusrc, demultiplexer_1_out1, demultiplexer_1_out2, demultiplexer_1_out3, demultiplexer_1_out6, incPC,
       ldImmed, ldInstr, ldPC, or_1_out, or_2_out, wreg, wrflags;
  wire [1:0] addrsel, dsel, regsrc, ssel;
  wire [2:0] AluOp, bussel;
  wire [7:0] alu_1_flags_2, alu_1_result, databus, dbus, flags, imbus, IR_q, multiplexer_1_out,
       multiplexer_2_out, pcbus, sbus;

  Control control_1 (
    .wrMemory(wrMemory), .wrOutput(wrOutput), .addrsel(addrsel), .bussel(bussel), .alusrc(alusrc),
    .regsrc(regsrc), .ssel(ssel), .dsel(dsel), .ldImmed(ldImmed), .ldPC(ldPC), .incPC(incPC), .wreg(wreg),
    .AluOp(AluOp), .Clk(Clk), .InRdy(InRdy), .OutRdy(OutRdy), .ldInstr(ldInstr), .instr(IR_q),
    .wrflags(wrflags), .flags(flags));
  Register IR (.D(databus), .en(ldInstr), .Q(IR_q), .clk(Clk));  // open: clr
  Register Immed (.D(databus), .en(ldImmed), .Q(imbus), .clk(Clk));  // open: clr
  Multiplexer #(.select(2), .width(8), .enable("false")) multiplexer_1 (
    .in0(sbus), .in1(alu_1_result), .in2(imbus), .in3(databus), .out(multiplexer_1_out), .sel(regsrc));
  Counter PC (.load(ldPC), .D(imbus), .count(incPC), .Q(pcbus), .clk(Clk));  // open: carry, clr
  Multiplexer #(.width(8), .enable("false")) multiplexer_2 (
    .in0(sbus), .in1(databus), .out(multiplexer_2_out), .sel(alusrc));
  Registers R0___R3 (.ssel(ssel), .dsel(dsel), .D(multiplexer_1_out), .wrD(wreg), .s(sbus), .d_2(dbus), .Clk(Clk));
  Demultiplexer #(.select(3), .enable("false")) demultiplexer_1 (
    .out1(demultiplexer_1_out1), .out2(demultiplexer_1_out2), .out3(demultiplexer_1_out3), .out4(dbussel[0]),
    .out5(dbussel[1]), .out6(demultiplexer_1_out6), .in(1'b1), .sel(bussel));  // open: out0, out7
  assign databus = demultiplexer_1_out1 ? 8'h1 : 8'bz;  // Controlled_Buffer controlled_buffer_1
  assign databus = demultiplexer_1_out6 ? pcbus : 8'bz;  // Controlled_Buffer controlled_buffer_2
  Multiplexer #(.select(2), .width(8), .enable("false")) multiplexer_3 (
    .in0(sbus), .in1(dbus), .in2(imbus), .in3(pcbus), .out(abus), .sel(addrsel));
  ALU alu_1 (
    .flags(flags), .a(multiplexer_2_out), .b(dbus), .result(alu_1_result), .OpSel(AluOp),
    .flags_2(alu_1_flags_2));
  Flags u_Flags (.flags(alu_1_flags_2), .wr__when_1__write_flags(wrflags), .Clk(Clk), .flags_2(flags));
  assign databus = demultiplexer_1_out2 ? sbus : 8'bz;  // Controlled_Buffer controlled_buffer_3
  assign databus = demultiplexer_1_out3 ? dbus : 8'bz;  // Controlled_Buffer controlled_buffer_4
  assign dbusout = or_1_out ? databus : 8'bz;  // Controlled_Buffer controlled_buffer_5
  assign databus = or_2_out ? dbusin : 8'bz;  // Controlled_Buffer controlled_buffer_6
  or or_1 (or_1_out, wrMemory, wrOutput);
  or or_2 (or_2_out, dbussel[0], dbussel[1]);

  // Other names for the same wires on the sheet: wrOutPort = wrOutput
endmodule

module Registers (
  input  [1:0] ssel,
  input  [1:0] dsel,
  input  [7:0] D,
  input  wrD,
  input  Clk,
  output [7:0] s,
  output [7:0] d_2
);

  wire demultiplexer_1_out0, demultiplexer_1_out1, demultiplexer_1_out2, demultiplexer_1_out3;
  wire [7:0] R0_q, R1_q, R2_q, R3_q;

  Demultiplexer #(.select(2), .enable("false")) demultiplexer_1 (
    .out0(demultiplexer_1_out0), .out1(demultiplexer_1_out1), .out2(demultiplexer_1_out2),
    .out3(demultiplexer_1_out3), .in(wrD), .sel(dsel));
  Register R0 (.D(D), .en(demultiplexer_1_out0), .Q(R0_q), .clk(Clk));  // open: clr
  Register R2 (.D(D), .en(demultiplexer_1_out2), .Q(R2_q), .clk(Clk));  // open: clr
  Register R1 (.D(D), .en(demultiplexer_1_out1), .Q(R1_q), .clk(Clk));  // open: clr
  Register R3 (.D(D), .en(demultiplexer_1_out3), .Q(R3_q), .clk(Clk));  // open: clr
  Multiplexer #(.select(2), .width(8), .enable("false")) multiplexer_1 (
    .in0(R0_q), .in1(R1_q), .in2(R2_q), .in3(R3_q), .out(s), .sel(ssel));
  Multiplexer #(.select(2), .width(8), .enable("false")) multiplexer_2 (
    .in0(R0_q), .in1(R1_q), .in2(R2_q), .in3(R3_q), .out(d_2), .sel(dsel));
endmodule

module ALU (
  input  [2:0] OpSel,
  input  [7:0] flags,
  input  [7:0] a,
  input  [7:0] b,
  output [7:0] result,
  output [7:0] flags_2
);

  wire [7:0] adder_1_out, subtractor_1_out;

  Adder adder_1 (.a(a), .b(b), .out(adder_1_out), .cin(flags[0]), .cout(flags_2[0]));
  Subtractor subtractor_1 (.a(a), .b(b), .out(subtractor_1_out));  // open: bin, bout
  Multiplexer #(.select(3), .width(8), .enable("false")) multiplexer_1 (
    .in0(adder_1_out), .in1(subtractor_1_out), .out({flags_2[2], result[6:0]}), .sel(OpSel));  // open: in2, in3, in4, in5, in6, in7
  zero zero_1 (.D({flags_2[2], result[6:0]}), .z(flags_2[1]));

  assign flags_2[7:3] = flags[7:3];
  assign result[7] = flags_2[2];
endmodule

module zero (
  input  [7:0] D,
  output z
);

  wire or_1_out;

  or or_1 (or_1_out, D[0], D[1], D[2], D[3], D[4], D[5], D[6], D[7]);
  not not_1 (z, or_1_out);
endmodule

module Control (
  input  [7:0] flags,
  input  InRdy,
  input  OutRdy,
  input  [7:0] instr,
  input  Clk,
  output wrMemory,
  output wrOutput,
  output wreg,
  output ldPC,
  output ldImmed,
  output ldInstr,
  output incPC,
  output alusrc,
  output [1:0] ssel,
  output [1:0] dsel,
  output [1:0] regsrc,
  output [1:0] addrsel,
  output [2:0] bussel,
  output wrflags,
  output [2:0] AluOp
);

  wire and_1_out, if_0_out, if_c_out, if_s_out, ifn_0_out, ifn_c_out, ifn_s_out, not_1_out, not_2_out,
       or_1_out, s_r_ff_1_q;
  wire [1:0] Phase_q;
  wire [31:0] multiplexer_1_out, rom_1_data, rom_2_data, rom_3_data;
  wire [31:23] controlled_buffer_1_out;

  ROM #(.dataWidth(32)) rom_1 (.addr(instr), .data(rom_1_data));  // open: sel
  ROM #(.dataWidth(32)) rom_2 (.addr(instr), .data(rom_2_data));  // open: sel
  ROM #(.dataWidth(32)) rom_3 (.addr(instr), .data(rom_3_data));  // open: sel
  S_R_Flip_Flop #(.trigger("falling")) s_r_ff_1 (
    .S(controlled_buffer_1_out[31]), .clk(Clk), .R(s_r_ff_1_q), .Q(s_r_ff_1_q));  // open: Qn, preset, reset, en
  not not_1 (not_1_out, s_r_ff_1_q);
  Multiplexer #(.select(2), .width(32), .enable("false")) multiplexer_1 (
    .in0(32'h5c060), .in1(rom_1_data), .in2(rom_2_data), .in3(rom_3_data), .out(multiplexer_1_out),
    .sel(Phase_q));
  Counter #(.width(2), .max('h3)) Phase (
    .load(s_r_ff_1_q), .D(2'b00), .count(not_1_out), .Q(Phase_q), .clk(Clk));  // open: carry, clr
  and if_c (if_c_out, flags[0], multiplexer_1_out[30], multiplexer_1_out[27]);
  and ifn_c (ifn_c_out, ~flags[0], ~multiplexer_1_out[30], multiplexer_1_out[27]);  // AND_Gate
  and if_0 (if_0_out, flags[1], multiplexer_1_out[30], multiplexer_1_out[28]);
  and ifn_0 (ifn_0_out, ~flags[1], ~multiplexer_1_out[30], multiplexer_1_out[28]);  // AND_Gate
  and if_s (if_s_out, flags[2], multiplexer_1_out[30], multiplexer_1_out[29]);
  and ifn_s (ifn_s_out, ~flags[2], ~multiplexer_1_out[30], multiplexer_1_out[29]);  // AND_Gate
  or or_1 (or_1_out, if_c_out, ifn_c_out, if_0_out, ifn_0_out, if_s_out, ifn_s_out, and_1_out);
  and and_1 (and_1_out, ~multiplexer_1_out[29], ~multiplexer_1_out[28], ~multiplexer_1_out[27]);  // AND_Gate
  not not_2 (not_2_out, or_1_out);
  assign {controlled_buffer_1_out, AluOp, wrflags, bussel, addrsel, regsrc, dsel, ssel, alusrc, incPC, ldInstr, ldImmed, ldPC, wreg, wrOutput, wrMemory} = not_2_out ? 32'h80000000 : 32'bz;  // Controlled_Buffer controlled_buffer_1
  assign {controlled_buffer_1_out, AluOp, wrflags, bussel, addrsel, regsrc, dsel, ssel, alusrc, incPC, ldInstr, ldImmed, ldPC, wreg, wrOutput, wrMemory} = or_1_out ? multiplexer_1_out : 32'bz;  // Controlled_Buffer controlled_buffer_2

  // Other names for the same wires on the sheet: carry = flags[0]; zero = flags[1]; sign = flags[2]

  // Notes on the sheet:
  //   contents of rom_1 (hex, n*v repeats v):
  //   80000000 127*0 8005c050
  //   contents of rom_2 (hex, n*v repeats v):
  //   0 a0000008 118*0 2005c008
endmodule

module Flags (
  input  [7:0] flags,
  input  wr__when_1__write_flags,
  input  Clk,
  output [7:0] flags_2
);

  Register u_Flags (.D(flags), .en(wr__when_1__write_flags), .Q(flags_2), .clk(Clk));  // open: clr
endmodule
