// Logisim project 8bitComputerManualCTRL.circ as structural Verilog: 6 circuits, main circuit main
module main (
  input  Ready,
  input  Ready_2,
  input  [7:0] Input_Port,
  output [7:0] Output_Port
);

  wire clock_1_out, cpu_1_wrmemory, cpu_1_wroutput, demultiplexer_1_out1, demultiplexer_1_out2;
  wire [1:0] cpu_1_dbussel;
  wire [7:0] controlled_buffer_3_out, cpu_1_abus, cpu_1_dbusout, ram_1_data;

  Clock clock_1 (.out(clock_1_out));
  Demultiplexer #(.select(2), .enable("false")) demultiplexer_1 (
    .out1(demultiplexer_1_out1), .out2(demultiplexer_1_out2), .in(1'b1), .sel(cpu_1_dbussel));  // open: out0, out3
  CPU cpu_1 (
    .Clk(clock_1_out), .InRdy(Ready), .OutRdy(Ready_2), .dbusout(cpu_1_dbusout), .abus(cpu_1_abus),
    .dbussel(cpu_1_dbussel), .wrMemory(cpu_1_wrmemory), .wrOutput(cpu_1_wroutput), .dbusin(cpu_1_dbusout));
  assign cpu_1_dbusout = demultiplexer_1_out1 ? Input_Port : 8'bz;  // Controlled_Buffer controlled_buffer_1
  assign Output_Port = cpu_1_wroutput ? cpu_1_dbusout : 8'bz;  // Controlled_Buffer controlled_buffer_2
  assign controlled_buffer_3_out = cpu_1_wrmemory ? cpu_1_dbusout : 8'bz;  // Controlled_Buffer controlled_buffer_3
  assign cpu_1_dbusout = demultiplexer_1_out2 ? ram_1_data : 8'bz;  // Controlled_Buffer controlled_buffer_4
  RAM #(.bus("separate")) ram_1 (
    .addr(cpu_1_abus), .din(controlled_buffer_3_out), .data(ram_1_data), .str(cpu_1_wrmemory), .sel(1'b1),
    .clk(clock_1_out), .ld(demultiplexer_1_out2));  // open: clr

  // Notes on the sheet:
  //   Addressbus
  //   Datenbus
endmodule

module CPU (
  input  InRdy,
  input  OutRdy,
  input  [7:0] dbusin,
  input  Clk,
  output [7:0] abus,
  output wrMemory,
  output wrOutput,
  output [7:0] dbusout,
  output [1:0] dbussel
);

  wire alusrc, demultiplexer_1_out1, demultiplexer_1_out2, demultiplexer_1_out3, demultiplexer_1_out6, incPC,
       ldImmed, ldInstr, ldPC, or_1_out, or_2_out, wreg, wrflags;
  wire [1:0] addrsel, dsel, regsrc, ssel;
  wire [2:0] AluOp, bussel;
  wire [7:0] alu_1_flags_2, alu_1_result, databus, dbus, flags, imbus, multiplexer_1_out, multiplexer_2_out,
       pcbus, sbus;

  Register #(.width(1)) register_1 (.Q(wrMemory));  // open: D, en, clk, clr
  Register #(.width(1)) register_2 (.Q(wrOutput));  // open: D, en, clk, clr
  Register #(.width(2)) register_3 (.Q(addrsel));  // open: D, en, clk, clr
  Register #(.width(3)) register_4 (.Q(bussel));  // open: D, en, clk, clr
  Register #(.width(1)) register_5 (.Q(alusrc));  // open: D, en, clk, clr
  Register #(.width(2)) register_6 (.Q(regsrc));  // open: D, en, clk, clr
  Register #(.width(2)) register_7 (.Q(ssel));  // open: D, en, clk, clr
  Register #(.width(2)) register_8 (.Q(dsel));  // open: D, en, clk, clr
  Register #(.width(1)) register_9 (.Q(ldImmed));  // open: D, en, clk, clr
  Register #(.width(1)) register_10 (.Q(ldPC));  // open: D, en, clk, clr
  Register #(.width(1)) register_11 (.Q(incPC));  // open: D, en, clk, clr
  Register #(.width(1)) register_12 (.Q(wreg));  // open: D, en, clk, clr
  Register #(.width(3)) register_13 (.Q(AluOp));  // open: D, en, clk, clr
  Register #(.width(1)) register_14 (.Q(ldInstr));  // open: D, en, clk, clr
  Register #(.width(1)) register_15 (.Q(wrflags));  // open: D, en, clk, clr
  Register IR (.D(databus), .en(ldInstr), .clk(Clk));  // open: Q, clr
  Register Immed (.D(databus), .en(ldImmed), .Q(imbus), .clk(Clk));  // open: clr
  Multiplexer #(.select(2), .width(8), .enable("false")) multiplexer_1 (
    .in0(sbus), .in1(alu_1_result), .in2(imbus), .in3(databus), .out(multiplexer_1_out), .sel(regsrc));
  Counter PC (.load(ldPC), .D(imbus), .count(incPC), .Q(pcbus), .clk(Clk));  // open: carry, clr
  Multiplexer #(.width(8), .enable("false")) multiplexer_2 (
    .in0(sbus), .in1(databus), .out(multiplexer_2_out), .sel(alusrc));
  Registers R0___R3 (.ssel(ssel), .dsel(dsel), .D(multiplexer_1_out), .wrD(wreg), .s(sbus), .d_2(dbus), .Clk(Clk));
  Demultiplexer #(.select(3), .enable("false")) demultiplexer_1 (
    .out1(demultiplexer_1_out1), .out2(demultiplexer_1_out2), .out3(demultiplexer_1_out3), .out4(dbussel[0]),
    .out5(dbussel[1]), .out6(demultiplexer_1_out6), .in(1'b1), .sel(bussel));  // open: out0, out7
  assign databus = demultiplexer_1_out1 ? 8'h1 : 8'bz;  // Controlled_Buffer controlled_buffer_1
  assign databus = demultiplexer_1_out6 ? pcbus : 8'bz;  // Controlled_Buffer controlled_buffer_2
  Multiplexer #(.select(2), .width(8), .enable("false")) multiplexer_3 (
    .in0(sbus), .in1(dbus), .in2(imbus), .in3(pcbus), .out(abus), .sel(addrsel));
  ALU alu_1 (
    .OpSel(AluOp), .flags(flags), .a(multiplexer_2_out), .result(alu_1_result), .b(dbus),
    .flags_2(alu_1_flags_2));
  Flags u_Flags (.flags(alu_1_flags_2), .wr__when_1__write_flags(wrflags), .Clk(Clk), .flags_2(flags));
  assign databus = demultiplexer_1_out2 ? sbus : 8'bz;  // Controlled_Buffer controlled_buffer_3
  assign databus = demultiplexer_1_out3 ? dbus : 8'bz;  // Controlled_Buffer controlled_buffer_4
  assign dbusout = or_1_out ? databus : 8'bz;  // Controlled_Buffer controlled_buffer_5
  assign databus = or_2_out ? dbusin : 8'bz;  // Controlled_Buffer controlled_buffer_6
  or or_1 (or_1_out, wrMemory, wrOutput);
  or or_2 (or_2_out, dbussel[0], dbussel[1]);

  // Other names for the same wires on the sheet: wrOutPort = wrOutput
endmodule

module Registers (
  input  [1:0] ssel,
  input  [1:0] dsel,
  input  [7:0] D,
  input  wrD,
  input  Clk,
  output [7:0] s,
  output [7:0] d_2
);

  wire demultiplexer_1_out0, demultiplexer_1_out1, demultiplexer_1_out2, demultiplexer_1_out3;
  wire [7:0] R0_q, R1_q, R2_q, R3_q;

  Demultiplexer #(.select(2), .enable("false")) demultiplexer_1 (
    .out0(demultiplexer_1_out0), .out1(demultiplexer_1_out1), .out2(demultiplexer_1_out2),
    .out3(demultiplexer_1_out3), .in(wrD), .sel(dsel));
  Register R0 (.D(D), .en(demultiplexer_1_out0), .Q(R0_q), .clk(Clk));  // open: clr
  Register R2 (.D(D), .en(demultiplexer_1_out2), .Q(R2_q), .clk(Clk));  // open: clr
  Register R1 (.D(D), .en(demultiplexer_1_out1), .Q(R1_q), .clk(Clk));  // open: clr
  Register R3 (.D(D), .en(demultiplexer_1_out3), .Q(R3_q), .clk(Clk));  // open: clr
  Multiplexer #(.select(2), .width(8), .enable("false")) multiplexer_1 (
    .in0(R0_q), .in1(R1_q), .in2(R2_q), .in3(R3_q), .out(s), .sel(ssel));
  Multiplexer #(.select(2), .width(8), .enable("false")) multiplexer_2 (
    .in0(R0_q), .in1(R1_q), .in2(R2_q), .in3(R3_q), .out(d_2), .sel(dsel));
endmodule

module ALU (
  input  [2:0] OpSel,
  input  [7:0] flags,
  input  [7:0] a,
  input  [7:0] b,
  output [7:0] result,
  output [7:0] flags_2
);

  wire [7:0] adder_1_out, subtractor_1_out;

  Adder adder_1 (.a(a), .b(b), .out(adder_1_out), .cin(flags[0]), .cout(flags_2[0]));
  Subtractor subtractor_1 (.a(a), .b(b), .out(subtractor_1_out));  // open: bin, bout
  Multiplexer #(.select(3), .width(8), .enable("false")) multiplexer_1 (
    .in0(adder_1_out), .in1(subtractor_1_out), .out({flags_2[2], result[6:0]}), .sel(OpSel));  // open: in2, in3, in4, in5, in6, in7
  zero zero_1 (.D({flags_2[2], result[6:0]}), .z(flags_2[1]));

  assign flags_2[7:3] = flags[7:3];
  assign result[7] = flags_2[2];
endmodule

module zero (
  input  [7:0] D,
  output z
);

  wire or_1_out;

  or or_1 (or_1_out, D[0], D[1], D[2], D[3], D[4], D[5], D[6], D[7]);
  not not_1 (z, or_1_out);
endmodule

module Flags (
  input  [7:0] flags,
  input  wr__when_1__write_flags,
  input  Clk,
  output [7:0] flags_2
);

  Register u_Flags (.D(flags), .en(wr__when_1__write_flags), .Q(flags_2), .clk(Clk));  // open: clr
endmodule
