// Logisim project SuperSimpleCPU-MachineCode.circ as structural Verilog: 2 circuits, main circuit main
module main (
  input  [3:0] IN_PORT,
  input  LDOP
);

  wire clock_1_out, demultiplexer_1_out1, demultiplexer_1_out2, demultiplexer_1_out3, demultiplexer_1_out4,
       demultiplexer_2_out0, demultiplexer_2_out1, demultiplexer_2_out2, not_1_out, not_2_out, not_3_out,
       or_1_out, or_2_out;
  wire [1:0] counter_1_q;
  wire [3:0] adder_1_out, ADR_q, AKKU_q, ALUTMP_q, controlled_buffer_1_out, controlled_buffer_3_out, IP_q,
       IR_q;

  Demultiplexer #(.select(4)) demultiplexer_1 (
    .out1(demultiplexer_1_out1), .out2(demultiplexer_1_out2), .out3(demultiplexer_1_out3),
    .out4(demultiplexer_1_out4), .in(not_1_out), .sel(IR_q));  // open: out0, out5, out6, out7, out8, out9, out10, out11, out12, out13, out14, out15, en
  not not_1 (not_1_out, LDOP);
  assign controlled_buffer_1_out = demultiplexer_1_out2 ? AKKU_q : 4'bz;  // Controlled_Buffer controlled_buffer_1
  Register #(.width(4)) AKKU (.D(controlled_buffer_1_out), .en(or_1_out), .Q(AKKU_q), .clk(clock_1_out));  // open: clr
  or or_1 (or_1_out, demultiplexer_1_out4, demultiplexer_2_out1, demultiplexer_1_out1);
  Register #(.width(4)) IR (.D(controlled_buffer_1_out), .en(LDOP), .Q(IR_q), .clk(clock_1_out));  // open: clr
  Clock clock_1 (.out(clock_1_out));
  assign controlled_buffer_1_out = demultiplexer_1_out4 ? IN_PORT : 4'bz;  // Controlled_Buffer controlled_buffer_2
  Register #(.width(4)) ADR (.Q(ADR_q), .clk(clock_1_out));  // open: D, en, clr
  not not_2 (not_2_out, LDOP);
  or or_2 (or_2_out, demultiplexer_1_out2, LDOP, demultiplexer_1_out1, demultiplexer_2_out0);
  Adder #(.width(4)) adder_1 (.a(controlled_buffer_1_out), .b(AKKU_q), .out(adder_1_out));  // open: cin, cout
  assign controlled_buffer_3_out = not_2_out ? ADR_q : 4'bz;  // Controlled_Buffer controlled_buffer_3
  Demultiplexer #(.select(2)) demultiplexer_2 (
    .out0(demultiplexer_2_out0), .out1(demultiplexer_2_out1), .out2(demultiplexer_2_out2),
    .in(demultiplexer_1_out3), .sel(counter_1_q));  // open: out3, en
  Counter #(.width(2), .max('h3)) counter_1 (
    .count(demultiplexer_1_out3), .Q(counter_1_q), .clk(clock_1_out), .clr(demultiplexer_2_out2));  // open: load, D, carry
  assign controlled_buffer_1_out = demultiplexer_2_out1 ? ALUTMP_q : 4'bz;  // Controlled_Buffer controlled_buffer_4
  Register #(.width(4)) ALUTMP (
    .D(adder_1_out), .en(demultiplexer_2_out0), .Q(ALUTMP_q), .clk(clock_1_out));  // open: clr
  assign controlled_buffer_3_out = LDOP ? IP_q : 4'bz;  // Controlled_Buffer controlled_buffer_5
  Counter #(.width(4), .max('hf)) IP (.count(LDOP), .Q(IP_q), .clk(clock_1_out));  // open: load, D, carry, clr
  not not_3 (not_3_out, demultiplexer_1_out2);
  RAM #(.addrWidth(4), .dataWidth(4)) ram_1 (
    .addr(controlled_buffer_3_out), .data(controlled_buffer_1_out), .sel(or_2_out), .clk(clock_1_out),
    .ld(not_3_out));  // open: clr

  // Notes on the sheet:
  //   1 = LDA
  //   2 = STA
  //   3 = ADD
  //   4 = INP
  //   PC
endmodule

module test (
  input  in_1,
  input  [3:0] in_2,
  input  in_3
);

  wire clock_1_out, not_1_out;
  wire [3:0] controlled_buffer_1_out, controlled_buffer_3_out, register_1_q, register_2_q;

  assign controlled_buffer_1_out = not_1_out ? in_2 : 4'bz;  // Controlled_Buffer controlled_buffer_1
  not not_1 (not_1_out, in_1);
  assign controlled_buffer_1_out = in_1 ? register_1_q : 4'bz;  // Controlled_Buffer controlled_buffer_2
  Register #(.width(4)) register_1 (.D(controlled_buffer_3_out), .Q(register_1_q), .clk(clock_1_out));  // open: en, clr
  Register #(.width(4)) register_2 (.D(controlled_buffer_1_out), .Q(register_2_q), .clk(clock_1_out));  // open: en, clr
  Clock clock_1 (.out(clock_1_out));
  assign controlled_buffer_3_out = in_3 ? register_2_q : 4'bz;  // Controlled_Buffer controlled_buffer_3
endmodule
