// Logisim project SuperSimpleCPU.circ as structural Verilog: 2 circuits, main circuit main
module main (
  input  [3:0] IN_PORT,
  input  LDA,
  input  STA,
  input  ADD,
  input  INP
);

  wire clock_1_out, demultiplexer_1_out0, demultiplexer_1_out1, demultiplexer_1_out2, not_1_out, or_1_out,
       or_2_out;
  wire [1:0] counter_1_q;
  wire [3:0] adder_1_out, ADR_q, AKKU_q, ALUTMP_q, controlled_buffer_1_out;

  assign controlled_buffer_1_out = STA ? AKKU_q : 4'bz;  // Controlled_Buffer controlled_buffer_1
  Register #(.width(4)) AKKU (.D(controlled_buffer_1_out), .en(or_1_out), .Q(AKKU_q), .clk(clock_1_out));  // open: clr
  or or_1 (or_1_out, INP, demultiplexer_1_out1, LDA);
  Clock clock_1 (.out(clock_1_out));
  assign controlled_buffer_1_out = INP ? IN_PORT : 4'bz;  // Controlled_Buffer controlled_buffer_2
  or or_2 (or_2_out, STA, LDA, demultiplexer_1_out0);
  Adder #(.width(4)) adder_1 (.a(controlled_buffer_1_out), .b(AKKU_q), .out(adder_1_out));  // open: cin, cout
  Register #(.width(4)) ADR (.Q(ADR_q), .clk(clock_1_out));  // open: D, en, clr
  Demultiplexer #(.select(2)) demultiplexer_1 (
    .out0(demultiplexer_1_out0), .out1(demultiplexer_1_out1), .out2(demultiplexer_1_out2), .in(ADD),
    .sel(counter_1_q));  // open: out3, en
  Counter #(.width(2), .max('h3)) counter_1 (
    .count(ADD), .Q(counter_1_q), .clk(clock_1_out), .clr(demultiplexer_1_out2));  // open: load, D, carry
  assign controlled_buffer_1_out = demultiplexer_1_out1 ? ALUTMP_q : 4'bz;  // Controlled_Buffer controlled_buffer_3
  Register #(.width(4)) ALUTMP (
    .D(adder_1_out), .en(demultiplexer_1_out0), .Q(ALUTMP_q), .clk(clock_1_out));  // open: clr
  not not_1 (not_1_out, STA);
  RAM #(.addrWidth(4), .dataWidth(4)) ram_1 (
    .addr(ADR_q), .data(controlled_buffer_1_out), .sel(or_2_out), .clk(clock_1_out), .ld(not_1_out));  // open: clr
endmodule

module test (
  input  in_1,
  input  [3:0] in_2,
  input  in_3
);

  wire clock_1_out, not_1_out;
  wire [3:0] controlled_buffer_1_out, controlled_buffer_3_out, register_1_q, register_2_q;

  assign controlled_buffer_1_out = not_1_out ? in_2 : 4'bz;  // Controlled_Buffer controlled_buffer_1
  not not_1 (not_1_out, in_1);
  assign controlled_buffer_1_out = in_1 ? register_1_q : 4'bz;  // Controlled_Buffer controlled_buffer_2
  Register #(.width(4)) register_1 (.D(controlled_buffer_3_out), .Q(register_1_q), .clk(clock_1_out));  // open: en, clr
  Register #(.width(4)) register_2 (.D(controlled_buffer_1_out), .Q(register_2_q), .clk(clock_1_out));  // open: en, clr
  Clock clock_1 (.out(clock_1_out));
  assign controlled_buffer_3_out = in_3 ? register_2_q : 4'bz;  // Controlled_Buffer controlled_buffer_3
endmodule
